# Fritzing sketch Wiring (saved by Fritzing 0.9.3b)

parts:
  Parça1 = NRF24L01+ Breakout Board
  Parça2 = NRF24L01+ Breakout Board
  Parça3 = Arduino Nano (Rev3.0) (ICSP)
  S11 = Round Pushbutton
  S12 = Round Pushbutton
  S13 = Round Pushbutton
  S14 = Round Pushbutton
  S15 = Round Pushbutton
  S16 = Round Pushbutton
  S17 = Round Pushbutton
  S18 = Round Pushbutton
  S19 = Round Pushbutton
  S20 = Round Pushbutton
  S21 = Round Pushbutton
  S22 = Round Pushbutton
  S23 = Round Pushbutton
  S24 = Round Pushbutton
  S25 = Round Pushbutton
  Parça4 = PowerBoost 500 Charger
  BAT1 = LIPO-110mAh [package=lipo-110]
  Parça5 = Arduino Leonardo (Rev3b)
  C1 = Electrolytic Capacitor [capacitance=100nF package="100 mil [THT, electrolytic]"]
  C2 = Electrolytic Capacitor [capacitance=100nF package="100 mil [THT, electrolytic]"]

nets:
  GND: Parça1.GND, Parça5.GND, C1.-
  VCC: Parça1.VCC, Parça5.3V3, C1.+
  N1: Parça1.CE, Parça5.D7
  N2: Parça1.CS, Parça5.D8/A8
  N3: Parça2.GND, C2.-
  VCC_2: Parça2.VCC, Parça3.3V3, C2.+
  N4: Parça2.CE, Parça3.D9
  N5: Parça2.CS, Parça3.D10
  N6: Parça2.SCK, Parça3.D13/SCK
  N7: Parça2.MOSI, Parça3.D11/MOSI
  N8: Parça2.MISO, Parça3.D12/MISO
  N9: Parça3.GND, S11.leg0, S18.leg0
  N10: Parça3.D2, S15.leg0
  N11: Parça3.D3, S16.leg0
  N12: Parça3.D4, S17.leg0
  N13: Parça3.D5, S11.leg1
  N14: Parça3.D6, S14.leg1
  N15: Parça3.D7, S13.leg1
  N16: Parça3.D8, S12.leg1
  N17: Parça3.VIN, Parça4.5.0V
  N18: Parça3.A7, S25.leg0
  N19: Parça3.A6, S24.leg1
  N20: Parça3.A5, S23.leg0
  N21: Parça3.A4, S22.leg0
  N22: Parça3.A3, S21.leg0
  N23: Parça3.A2, S18.leg1
  N24: Parça3.A1, S19.leg1
  N25: Parça3.A0, S20.leg1
  N26: Parça4.VBAT_OUT, BAT1.+
  N27: Parça4.GND, BAT1.-

notes:
  Step Up Modul 18650
  Bat+ Bat- Girişlerine
  Step Up
  V out +
  V out -
  Çıkış 7V
  Nrf24 3.3 v ile beslenecektir.!!
  ALICI
  VERİCİ
